# Fritzing sketch SlideProjector_ArduinoControlled_relay_Electronics_skematics (saved by Fritzing 0.9.3b)
breadboards: 1

parts:
  VCC1 = Battery block 9V
  Q1 = Basic FET N-Channel [package="DPak [SMD]"]
  R1 = Resistor [tolerance=±5% resistance=10k package="0603 [SMD]"]
  Part1 = Arduino Uno (Rev3)
  U1 = SWITCH_SPDT [package=kps-1290]
  8-pin_relay_JRC-19F = IC, DIP package, 8 pins [chip_label=IC]
  LED1 = smd LED [color="Red (633nm)" package="0603 [SMD]"]
  R2 = Resistor [tolerance=±5% resistance=10k package="0603 [SMD]"]

nets:
  N1: VCC1.-, Q1.source, Part1.GND, R2.Pin_1
  N2: VCC1.+, U1.O, 8-pin_relay_JRC-19F.pin7, 8-pin_relay_JRC-19F.pin8
  N3: Q1.Gate, R1.Pin_1
  N4: Q1.drain, 8-pin_relay_JRC-19F.pin1
  N5: R1.Pin_0, Part1.D13/SCK
  N6: Part1.VIN, U1.S
  N7: 8-pin_relay_JRC-19F.pin5, LED1.anode
  N8: LED1.cathode, R2.Pin_0
