# Fritzing sketch FlickeringLEDLight_skematics (saved by Fritzing 0.9.3b)
breadboards: 1

parts:
  Q1 = Basic FET N-Channel [package="DPak [SMD]"]
  R1 = Resistor [tolerance=±5% resistance=10k package="0603 [SMD]"]
  Part1 = Arduino Uno (Rev3)
  LED1 = smd LED [color="Red (633nm)" package="0603 [SMD]"]
  VCC1 = Battery block 9V

nets:
  N1: Q1.Gate, R1.Pin_1
  N2: Q1.drain, LED1.cathode
  N3: Q1.source, Part1.GND, VCC1.-
  N4: R1.Pin_0, Part1.D9_PWM
  N5: LED1.anode, VCC1.+
